# Fritzing sketch FinalPhase4Wiring (saved by Fritzing 1.0.1rc)
circuit board: 8.46667cm x 5.64444cm
breadboards: 1

parts:
  J1 = Raspberry Pi Header 40pin [form="♂ (male)" package=THT]
  R2 = Resistor [tolerance=±5% power=0.25W resistance=220 package=THT]
  M1 = DC Motor [voltage_(max)=6V voltage_(min)=3V]
  Mod1 = Amica NodeMCU DEVKIT 1.0
  VCC1 = Battery block 9V
  R1 = Resistor [tolerance=±5% resistance=220 package="0402 [SMD]"]
  R3 = Resistor [tolerance=±5% power=0.25W resistance=220 package=THT]
  LED3 = LED - 5mm [color="Red (633nm)" current=0.030A package="5 mm [THT]"]
  J2 = Raspberry Pi Header 40pin [form="♂ (male)" package=THT]
  LED2 = LED - 5mm [color="Red (633nm)" current=0.030A package="5 mm [THT]"]
  RHT1 = Humidity and Temperature Sensor RHT03
  IC1 = L293D [package=THT]

nets (from the schematic view):
  N1: J1.GIPO12, R2.Pin_0
  N2: R2.Pin_1, LED2.anode
  3V3: M1.pin_2, VCC1.-, R1.Pin_0, R1.Pin_1, J2.3v3, J2.GIPO22, J2.3V3, RHT1.Data-signal, RHT1.GND_2, IC1.Enable_1
  N3: Mod1.pin1, Mod1.pin_10, Mod1.pin_26, LED3.anode
  N4: Mod1.pin2, Mod1.pin_9, Mod1.pin_25, Mod1.pin_29
  N5: Mod1.pin_16, R3.Pin_1, LED3.cathode
  N6: VCC1.+, IC1.+V
  N7: J2.GND, J2.GIPO27, J2.GIPO5
  N8: J2.GIPO17, IC1.+Vmotor
  N9: IC1.Out_1_(_Controlled_by_Enable_1_), IC1.0V
  N10: IC1.Out_2_(_Controlled_by_Enable_1_), IC1.In_2

custom parts:
  Raspberry Pi Header 40pin: Raspberry Pi 40 pin header - for creating your own shields.
